// Logisim project riscv.circ as structural Verilog: 28 circuits, main circuit RISCV32
module RISCV32 (
);

  wire bypass_black_box_1_p3, clk, computeaddress_1_p3, computeaddress_1_p4, decode_1_regwe, decode_1_set,
       decode_1_setsign, decode_1_shiftbyregval, decode_1_useimm, decode_1_usepc, decode_1_zeroouta,
       detectpc_stall_nop_1_dxnop, detectpc_stall_nop_1_stallwe, detectpc_stall_nop_1_usenewpc,
       dx_1_auipcout, dx_1_regweout, dx_1_setout, dx_1_setsignout, dx_1_shiftregvalout, dx_1_useimmout,
       dx_1_zerooutaout, memflags_1_ld, memflags_1_str, mw_1_datactrl, not_1_out, ram_1_p7,
       registerfile_1_p3, xm_1_ldflagout, xm_1_strflagout;
  wire [1:0] bypass_black_box_1_p7, bypass_black_box_1_p8;
  wire [3:0] decode_1_aluop, decode_1_selectbytes, dx_1_aluopout, dx_1_selectbytesout, xm_1_selectbytesout;
  wire [4:0] bypass_black_box_1_p4, decode_1_rd, decode_1_rs1, decode_1_rs2, dx_1_rdout, dx_1_rs1out,
       dx_1_rs1out_2, registerfile_1_p4;
  wire [11:0] decode_1_tableb, dx_1_tablebout;
  wire [31:0] compare_1_result, decode_1_imm, dx_1_aout, dx_1_bout, dx_1_immout, dx_1_nextpcout, dx_1_pcout,
       execute_1_memdata, execute_1_nextpcout, execute_1_result, fd_1_instout, fd_1_pcout,
       increment_pc_1_out_2, increment_pc_2_out_2, jumphandler_1_branchtarget, jumphandler_1_resultout,
       multiplexer_1_out, multiplexer_2_out, mux3to1_1_out_5, mux3to1_2_out_5, mw_1_dataout, mw_1_resultout,
       register_1_q, registerfile_1_p1, registerfile_1_p7, registerfile_1_p8, risc_vprogramrom_1_p2,
       signextendlb_1_p4, xm_1_dataout, xm_1_resultout;

  Clock clock_1 (.out(clk));
  Register #(.width(32)) register_1 (
    .D(multiplexer_1_out), .en(detectpc_stall_nop_1_stallwe), .clk(clk), .Q(register_1_q));  // open: clr
  Increment_PC increment_pc_1 (.in_1(register_1_q), .out_2(increment_pc_1_out_2));
  Multiplexer #(.width(32), .enable("false")) multiplexer_1 (
    .in0(increment_pc_1_out_2), .in1(jumphandler_1_branchtarget), .out(multiplexer_1_out),
    .sel(detectpc_stall_nop_1_usenewpc));
  // RISC_VProgramROM risc_vprogramrom_1: pin names not known; wires that end beside it: register_1_q, risc_vprogramrom_1_p2
  FD fd_1 (
    .inst(risc_vprogramrom_1_p2), .instOut(fd_1_instout), .PC(register_1_q), .clk(clk),
    .stallWE(detectpc_stall_nop_1_stallwe), .nop(detectpc_stall_nop_1_usenewpc), .PCout(fd_1_pcout));
  not not_1 (not_1_out, clk);
  Decode decode_1 (
    .shiftbyregval(decode_1_shiftbyregval), .rd(decode_1_rd), .instr(fd_1_instout), .rs2(decode_1_rs2),
    .set(decode_1_set), .ALUop(decode_1_aluop), .imm(decode_1_imm), .rs1(decode_1_rs1),
    .regWE(decode_1_regwe), .tableB(decode_1_tableb), .useImm(decode_1_useimm), .setsign(decode_1_setsign),
    .usePC(decode_1_usepc), .ZeroOutA(decode_1_zeroouta), .SelectBytes(decode_1_selectbytes));
  Increment_PC increment_pc_2 (.in_1(fd_1_pcout), .out_2(increment_pc_2_out_2));
  // RegisterFile registerfile_1: pin names not known; wires that end beside it: registerfile_1_p1, not_1_out, registerfile_1_p3, registerfile_1_p4, decode_1_rs1, decode_1_rs2, registerfile_1_p7, registerfile_1_p8
  DX dx_1 (
    .shiftRegVal(decode_1_shiftbyregval), .setSignOut(dx_1_setsignout), .selectBytesOut(dx_1_selectbytesout),
    .tableBout(dx_1_tablebout), .regWE(decode_1_regwe), .AUIPCout(dx_1_auipcout), .useImm(decode_1_useimm),
    .ALUopOut(dx_1_aluopout), .setOut(dx_1_setout), .rdOut(dx_1_rdout), .selectBytes(decode_1_selectbytes),
    .useImmOut(dx_1_useimmout), .ZeroOutAout(dx_1_zerooutaout), .shiftRegValOut(dx_1_shiftregvalout),
    .immOut(dx_1_immout), .regWEout(dx_1_regweout), .tableB(decode_1_tableb), .imm(decode_1_imm),
    .rd(decode_1_rd), .AUIPC(decode_1_usepc), .setSign(decode_1_setsign), .set(decode_1_set),
    .ALUop(decode_1_aluop), .ZeroOutA(decode_1_zeroouta), .rs1(decode_1_rs1), .rs1out(dx_1_rs1out),
    .rs1_2(decode_1_rs2), .rs1out_2(dx_1_rs1out_2), .B(registerfile_1_p7), .Bout(dx_1_bout),
    .A(registerfile_1_p8), .Aout(dx_1_aout), .PC(fd_1_pcout), .PCout(dx_1_pcout),
    .nop(detectpc_stall_nop_1_dxnop), .clk(clk), .nextPC(increment_pc_2_out_2), .nextPCout(dx_1_nextpcout));
  // Bypass_Black_Box bypass_black_box_1: pin names not known; wires that end beside it: dx_1_rs1out, dx_1_rs1out_2, bypass_black_box_1_p3, bypass_black_box_1_p4, registerfile_1_p3, registerfile_1_p4, bypass_black_box_1_p7, bypass_black_box_1_p8
  MUX3to1 mux3to1_1 (
    .out_5(mux3to1_1_out_5), .ME(xm_1_resultout), .WB(registerfile_1_p1), .EX(dx_1_bout),
    .Sel(bypass_black_box_1_p7));
  MUX3to1 mux3to1_2 (
    .out_5(mux3to1_2_out_5), .ME(xm_1_resultout), .WB(registerfile_1_p1), .EX(dx_1_aout),
    .Sel(bypass_black_box_1_p8));
  Compare compare_1 (
    .A(mux3to1_1_out_5), .B(mux3to1_2_out_5), .imm(dx_1_immout), .useImm(dx_1_useimmout),
    .SetSign(dx_1_setsignout), .result(compare_1_result));
  Execute execute_1 (
    .UsePC(dx_1_auipcout), .rB(dx_1_rs1out_2), .B(mux3to1_2_out_5), .ZeroA(dx_1_zerooutaout),
    .imm(dx_1_immout), .A(mux3to1_1_out_5), .ALUop(dx_1_aluopout), .PC(dx_1_pcout),
    .shiftbyregval(dx_1_shiftregvalout), .memData(execute_1_memdata), .useImm(dx_1_useimmout),
    .result(execute_1_result), .nextPC(dx_1_nextpcout), .nextPCout(execute_1_nextpcout));
  detectPC_Stall_nop detectpc_stall_nop_1 (
    .tableB(dx_1_tablebout), .useNewPC(detectpc_stall_nop_1_usenewpc), .D_X_rd(dx_1_rdout),
    .A(mux3to1_1_out_5), .F_D_rs1(decode_1_rs1), .stallWE(detectpc_stall_nop_1_stallwe), .B(mux3to1_2_out_5),
    .F_D_rs2(decode_1_rs2), .DXnop(detectpc_stall_nop_1_dxnop));
  Multiplexer #(.width(32), .enable("false")) multiplexer_2 (
    .in0(execute_1_result), .in1(compare_1_result), .out(multiplexer_2_out), .sel(dx_1_setout));
  MemFlags memflags_1 (.TableB(dx_1_tablebout), .ld(memflags_1_ld), .str(memflags_1_str));
  jumpHandler jumphandler_1 (
    .resultOut(jumphandler_1_resultout), .result(multiplexer_2_out), .tableBOneHot(dx_1_tablebout),
    .branchTarget(jumphandler_1_branchtarget), .nextPC(execute_1_nextpcout));
  XM xm_1 (
    .rdOut(bypass_black_box_1_p4), .selectBytes(dx_1_selectbytesout), .selectBytesOut(xm_1_selectbytesout),
    .ldFlag(memflags_1_ld), .strFlag(memflags_1_str), .resultOut(xm_1_resultout),
    .result(jumphandler_1_resultout), .regWEout(bypass_black_box_1_p3), .rd(dx_1_rdout),
    .ldFlagOut(xm_1_ldflagout), .regWE(dx_1_regweout), .strFlagout(xm_1_strflagout), .clk(clk),
    .data(execute_1_memdata), .dataOut(xm_1_dataout));
  // computeAddress computeaddress_1: pin names not known; wires that end beside it: xm_1_resultout, xm_1_selectbytesout, computeaddress_1_p3, computeaddress_1_p4, xm_1_dataout
  // RAM ram_1: pin names not known; wires that end beside it: computeaddress_1_p3, xm_1_dataout, xm_1_strflagout, computeaddress_1_p4, clk, xm_1_ldflagout, ram_1_p7
  // SignExtendLB signextendlb_1: pin names not known; wires that end beside it: ram_1_p7, xm_1_ldflagout, computeaddress_1_p4, signextendlb_1_p4
  MW mw_1 (
    .regWEout(registerfile_1_p3), .regWE(bypass_black_box_1_p3), .data(signextendlb_1_p4),
    .rdOut(registerfile_1_p4), .dataOut(mw_1_dataout), .rd(bypass_black_box_1_p4), .result(xm_1_resultout),
    .resultOut(mw_1_resultout), .clk(clk), .ldFlag(xm_1_ldflagout), .dataCtrl(mw_1_datactrl));
  Multiplexer #(.width(32), .enable("false")) multiplexer_3 (
    .in0(mw_1_resultout), .in1(mw_1_dataout), .out(registerfile_1_p1), .sel(mw_1_datactrl));

  // Notes on the sheet:
  //   contents of risc_vprogramrom_1 (hex, n*v repeats v):
  //   SW x5, 4(x0) LB x6, 4(x0) LW x7, 4(x0)
endmodule

module Increment_PC (
  input  [31:0] in_1,
  output [31:0] out_2
);

  // Incrementer #(.width(30)) incrementer_1: pin names not known; wires that end beside it: in_1[31:2], out_2[31:2]

  assign out_2[1:0] = in_1[1:0];
endmodule

module Decode (
  input  [31:0] instr,
  output [31:0] imm,
  output useImm,
  output [4:0] rs1,
  output [4:0] rs2,
  output [4:0] rd,
  output [3:0] ALUop,
  output [11:0] tableB,
  output regWE,
  output set,
  output shiftbyregval,
  output setsign,
  output usePC,
  output ZeroOutA,
  output [3:0] SelectBytes
);

  wire decode_black_box_1_p6, decode_black_box_1_p8, decode_black_box_1_p9, decode_black_box_1_p10,
       decode_black_box_1_p11, decode_black_box_1_p12, decode_black_box_1_p13, decode_black_box_1_p14,
       decode_black_box_1_p16, or_1_out, tablebdecode_1_tablebhot;
  wire [3:0] decode_black_box_1_p7;
  wire [4:0] decode_black_box_1_p2, decode_black_box_1_p3, decode_black_box_1_p4;
  wire [31:0] decode_black_box_1_p5, tablebdecode_1_imm;

  // Decode_Black_Box decode_black_box_1: pin names not known; wires that end beside it: instr, decode_black_box_1_p2, decode_black_box_1_p3, decode_black_box_1_p4, decode_black_box_1_p5, decode_black_box_1_p6, decode_black_box_1_p7, decode_black_box_1_p8, decode_black_box_1_p9, decode_black_box_1_p10, decode_black_box_1_p11, decode_black_box_1_p12, decode_black_box_1_p13, decode_black_box_1_p14, ZeroOutA, decode_black_box_1_p16, tableB[11], tableB[10], tableB[9], tableB[8], tableB[7], tableB[6], tableB[5], tableB[4], tableB[3]
  or or_1 (or_1_out, instr[4], ~instr[5]);  // OR_Gate
  or or_2 (set, decode_black_box_1_p11, decode_black_box_1_p10, decode_black_box_1_p9, decode_black_box_1_p8);
  or or_3 (SelectBytes[0], tableB[10], tableB[11], tableB[1], tableB[0]);
  or or_4 (SelectBytes[3], tableB[11], tableB[10]);
  or or_5 (shiftbyregval, decode_black_box_1_p12, decode_black_box_1_p13, decode_black_box_1_p14);
  or or_6 (setsign, decode_black_box_1_p9, decode_black_box_1_p8);
  or or_7 (usePC, decode_black_box_1_p16, tableB[9], tableB[7], tableB[6], tableB[5], tableB[4], tableB[3], tableB[2]);
  getRegWE getregwe_1 (.tableAregWE(or_1_out), .tableB(tableB), .regWE(regWE));
  Multiplexer #(.width(32), .enable("false")) multiplexer_1 (
    .in0(decode_black_box_1_p5), .in1(tablebdecode_1_imm), .out(imm), .sel(tablebdecode_1_tablebhot));
  TableBDecode tablebdecode_1 (
    .Inst(instr), .tableB(tableB), .Imm(tablebdecode_1_imm), .tableBHot(tablebdecode_1_tablebhot),
    .rs1(decode_black_box_1_p2), .rs2(decode_black_box_1_p3), .rd(decode_black_box_1_p4), .rdOut(rd),
    .rs2Out(rs2), .rs1Out(rs1), .ALUopout(ALUop), .ALUop(decode_black_box_1_p7));
  Multiplexer #(.enable("false")) multiplexer_2 (
    .in0(decode_black_box_1_p6), .in1(tablebdecode_1_tablebhot), .out(useImm), .sel(tablebdecode_1_tablebhot));

  assign SelectBytes[2:1] = {2{SelectBytes[3]}};

  // Notes on the sheet:
  //   AUIPC, branches, and JAL use PC in ALU
  //   note: mux for undefined useImm behavior
  //   LSB to MSB:
  //   SB, LB, BGEU, BLTU, BGE,
  //   BLT, BNE, BEQ, JALR, JAL
  //   SW, LW
endmodule

module Execute (
  input  [31:0] A,
  input  [31:0] B,
  input  [4:0] rB,
  input  [31:0] imm,
  input  useImm,
  input  [3:0] ALUop,
  input  shiftbyregval,
  input  UsePC,
  input  [31:0] PC,
  input  ZeroA,
  input  [31:0] nextPC,
  output [31:0] memData,
  output [31:0] result,
  output [31:0] nextPCout
);

  wire not_1_out;
  wire [4:0] multiplexer_3_out;
  wire [31:0] and_1_out, bit_extender_1_out, multiplexer_1_out, multiplexer_2_out, multiplexer_4_out;

  not not_1 (not_1_out, ZeroA);
  Multiplexer #(.width(32), .enable("false")) multiplexer_1 (.in0(B), .in1(imm), .out(multiplexer_1_out), .sel(useImm));
  assign bit_extender_1_out = {{31{not_1_out}}, not_1_out};  // Bit_Extender bit_extender_1
  Multiplexer #(.width(32), .enable("false")) multiplexer_2 (
    .in0(multiplexer_1_out), .in1(A), .out(multiplexer_2_out), .sel(shiftbyregval));
  Multiplexer #(.width(5), .enable("false")) multiplexer_3 (
    .in0(rB), .in1(B[4:0]), .out(multiplexer_3_out), .sel(shiftbyregval));
  Multiplexer #(.width(32), .enable("false")) multiplexer_4 (.in0(A), .in1(PC), .out(multiplexer_4_out), .sel(UsePC));
  assign and_1_out = multiplexer_4_out & bit_extender_1_out;  // AND_Gate and_1, 32 bits wide
  // ALU alu_1: pin names not known; wires that end beside it: and_1_out, multiplexer_2_out, ALUop, multiplexer_3_out, result

  assign memData = B;
  assign nextPCout = nextPC;
endmodule

module MUX3to1 (
  input  [1:0] Sel,
  input  [31:0] EX,
  input  [31:0] WB,
  input  [31:0] ME,
  output [31:0] out_5
);

  wire [31:0] multiplexer_1_out;

  Multiplexer #(.width(32), .enable("false")) multiplexer_1 (.in0(EX), .in1(WB), .out(multiplexer_1_out), .sel(Sel[0]));
  Multiplexer #(.width(32), .enable("false")) multiplexer_2 (
    .in0(multiplexer_1_out), .in1(ME), .out(out_5), .sel(Sel[1]));
endmodule

module TableBDecode (
  input  [4:0] rs1,
  input  [4:0] rs2,
  input  [4:0] rd,
  input  [3:0] ALUop,
  input  [11:0] tableB,
  input  [31:0] Inst,
  output [4:0] rs1Out,
  output [4:0] rs2Out,
  output [4:0] rdOut,
  output [3:0] ALUopout,
  output tableBHot,
  output [31:0] Imm
);

  wire [3:0] bit_extender_1_out;

  or or_1 (tableBHot, tableB[0], tableB[1], tableB[2], tableB[3], tableB[4], tableB[5], tableB[6], tableB[7], tableB[8], tableB[9], tableB[10], tableB[11]);
  Multiplexer #(.width(5), .enable("false")) multiplexer_1 (
    .in0(rs1), .in1(Inst[19:15]), .out(rs1Out), .sel(tableBHot));
  Multiplexer #(.width(5), .enable("false")) multiplexer_2 (
    .in0(rs2), .in1(Inst[24:20]), .out(rs2Out), .sel(tableBHot));
  Multiplexer #(.width(5), .enable("false")) multiplexer_3 (.in0(rd), .in1(Inst[11:7]), .out(rdOut), .sel(tableBHot));
  assign bit_extender_1_out = {{3{tableBHot}}, tableBHot};  // Bit_Extender bit_extender_1
  ImmFormatter immformatter_1 (.imm(Imm), .tableB(tableB), .inst(Inst));
  Multiplexer #(.width(4), .enable("false")) multiplexer_4 (
    .in0(ALUop), .in1(bit_extender_1_out), .out(ALUopout), .sel(tableBHot));

  // Notes on the sheet:
  //   i.e. if tableB, ALUop = 1111
  //   If tableB is active, an ADDI is necessary.
endmodule

module Imm0 (
  input  [31:0] OneHot,
  input  lb,
  input  sb,
  input  [31:0] inst,
  output Bit0
);

  wire multiplexer_1_out, or_1_out, or_2_out;

  or or_1 (or_1_out, OneHot[22], lb);
  or or_2 (or_2_out, sb, OneHot[23]);
  Multiplexer #(.enable("false")) multiplexer_1 (
    .in0(inst[4]), .in1(inst[20]), .out(multiplexer_1_out), .sel(or_1_out));
  Multiplexer #(.enable("false")) multiplexer_2 (.in0(multiplexer_1_out), .in1(inst[7]), .out(Bit0), .sel(or_2_out));
endmodule

module Imm1_4 (
  input  [31:0] OneHot,
  input  lb,
  input  sb,
  input  [31:0] inst,
  output [3:0] Bits1_4
);

  wire nor_1_out;

  // OR_Gate or_1 has open pins: in0=OneHot[23], in1=OneHot[27], in2=OneHot[28], in3=OneHot[29], in4=OneHot[30], in5=OneHot[31], in6=sb, out=open
  nor nor_1 (nor_1_out, OneHot[22], OneHot[24], OneHot[25], lb);
  Multiplexer #(.width(4), .enable("false")) multiplexer_1 (
    .in0(inst[24:21]), .in1({inst[8], inst[9], inst[10], inst[11]}), .out(Bits1_4), .sel(nor_1_out));
endmodule

module Imm5_10 (
  input  [31:0] inst,
  output [5:0] Bits5_10
);


  assign Bits5_10 = inst[30:25];
endmodule

module Imm11 (
  input  [31:0] OneHot,
  input  lb,
  input  sb,
  input  [31:0] inst,
  output Bit11
);

  wire multiplexer_1_out, or_1_out;

  Multiplexer #(.enable("false")) multiplexer_1 (
    .in0(inst[7]), .in1(inst[20]), .out(multiplexer_1_out), .sel(OneHot[24]));
  or or_1 (or_1_out, OneHot[22], OneHot[23], OneHot[25], lb, sb);
  Multiplexer #(.enable("false")) multiplexer_2 (.in0(multiplexer_1_out), .in1(inst[31]), .out(Bit11), .sel(or_1_out));
endmodule

module Imm12_19 (
  input  [31:0] OneHot,
  input  [31:0] inst,
  output [7:0] Bits12_19
);

  wire [7:0] bit_extender_1_out;

  assign bit_extender_1_out = {{7{inst[31]}}, inst[31]};  // Bit_Extender bit_extender_1
  Multiplexer #(.width(8), .enable("false")) multiplexer_1 (
    .in0(inst[19:12]), .in1(bit_extender_1_out), .out(Bits12_19), .sel(OneHot[25]));
endmodule

module Imm20_30 (
  input  [31:0] inst,
  output [11:0] Bits20_31
);

  assign Bits20_31 = {{11{inst[31]}}, inst[31]};  // Bit_Extender bit_extender_1
endmodule

module ImmFormatter (
  input  [31:0] inst,
  input  [11:0] tableB,
  output [31:0] imm
);

  wire and_1_out, and_2_out, and_3_out, and_4_out, or_1_out, or_2_out;
  wire [1:0] or_3_out;
  wire [11:0] loadandsaveimm_1_imm;
  wire [31:0] bit_extender_1_out, bit_extender_2_out, bit_extender_3_out, bit_extender_4_out;

  or or_1 (or_1_out, tableB[0], tableB[1], tableB[10], tableB[11]);
  or or_2 (or_2_out, tableB[2], tableB[3], tableB[4], tableB[5], tableB[6], tableB[7]);
  loadAndSaveImm loadandsaveimm_1 (.imm(loadandsaveimm_1_imm), .tableB(tableB), .instBits(inst));
  and and_1 (and_1_out, ~or_1_out, or_2_out, ~tableB[9], ~tableB[8]);  // AND_Gate
  or or_3 (or_3_out[0], and_1_out, and_2_out);
  and and_2 (and_2_out, ~or_1_out, ~or_2_out, ~tableB[9], tableB[8]);  // AND_Gate
  and and_3 (and_3_out, ~or_1_out, ~or_2_out, tableB[9], ~tableB[8]);  // AND_Gate
  or or_4 (or_3_out[1], and_3_out, and_4_out);
  and and_4 (and_4_out, ~or_1_out, ~or_2_out, ~tableB[9], tableB[8]);  // AND_Gate
  assign bit_extender_1_out = {{20{loadandsaveimm_1_imm[11]}}, loadandsaveimm_1_imm};  // Bit_Extender bit_extender_1
  assign bit_extender_2_out = {{19{inst[31]}}, {inst[31], inst[7], inst[30:25], inst[11:8], inst[2]}};  // Bit_Extender bit_extender_2
  assign bit_extender_3_out = {{11{inst[31]}}, {inst[31], inst[19:12], inst[20], inst[30:21], inst[4]}};  // Bit_Extender bit_extender_3
  assign bit_extender_4_out = {{20{inst[31]}}, inst[31:20]};  // Bit_Extender bit_extender_4
  Multiplexer #(.select(2), .width(32), .enable("false")) multiplexer_1 (
    .in0(bit_extender_1_out), .in1(bit_extender_2_out), .in2(bit_extender_3_out), .in3(bit_extender_4_out),
    .out(imm), .sel(or_3_out));

  // Notes on the sheet:
  //   LSB to MSB:
  //   SB, LB, BGEU, BLTU, BGE,
  //   BLT, BNE, BEQ, JALR, JAL
  //   SW, LW
  //   Loads and Saves
  //   Branches
  //   JAL
  //   JALR
  //   Load or Save
  //   Branch
  //   JAL
  //   JALR
endmodule

module detectPC_Stall_nop (
  input  [31:0] A,
  input  [31:0] B,
  input  [11:0] tableB,
  input  [4:0] F_D_rs1,
  input  [4:0] D_X_rd,
  input  [4:0] F_D_rs2,
  output useNewPC,
  output DXnop,
  output stallWE
);

  wire and_1_out, and_2_out, and_3_out, and_4_out, and_5_out, and_6_out, branchlogic_1_usenewpc, or_1_out,
       or_2_out, or_3_out, xnor_1_out, xnor_2_out, xnor_3_out, xnor_4_out, xnor_5_out, xnor_6_out,
       xnor_7_out, xnor_8_out, xnor_9_out, xnor_10_out;

  xnor xnor_1 (xnor_1_out, F_D_rs1[0], D_X_rd[0]);
  xnor xnor_2 (xnor_2_out, F_D_rs1[1], D_X_rd[1]);
  xnor xnor_3 (xnor_3_out, F_D_rs1[2], D_X_rd[2]);
  xnor xnor_4 (xnor_4_out, F_D_rs1[3], D_X_rd[3]);
  xnor xnor_5 (xnor_5_out, F_D_rs1[4], D_X_rd[4]);
  xnor xnor_6 (xnor_6_out, D_X_rd[0], F_D_rs2[0]);
  xnor xnor_7 (xnor_7_out, D_X_rd[1], F_D_rs2[1]);
  xnor xnor_8 (xnor_8_out, D_X_rd[2], F_D_rs2[2]);
  xnor xnor_9 (xnor_9_out, D_X_rd[3], F_D_rs2[3]);
  xnor xnor_10 (xnor_10_out, D_X_rd[4], F_D_rs2[4]);
  BranchLogic branchlogic_1 (.useNewPC(branchlogic_1_usenewpc), .B(B), .tableB(tableB), .A(A));
  or or_1 (or_1_out, tableB[9], tableB[8]);
  or or_2 (or_2_out, tableB[11], tableB[1]);
  and and_1 (and_1_out, ~F_D_rs1[0], ~F_D_rs1[1], ~F_D_rs1[2], ~F_D_rs1[3], ~F_D_rs1[4]);  // AND_Gate
  and and_2 (and_2_out, ~F_D_rs2[0], ~F_D_rs2[1], ~F_D_rs2[2], ~F_D_rs2[3], ~F_D_rs2[4]);  // AND_Gate
  and and_3 (and_3_out, and_4_out, ~and_1_out);  // AND_Gate
  and and_4 (and_4_out, or_2_out, xnor_1_out, xnor_2_out, xnor_3_out, xnor_4_out, xnor_5_out);
  and and_5 (and_5_out, and_6_out, ~and_2_out);  // AND_Gate
  and and_6 (and_6_out, or_2_out, xnor_6_out, xnor_7_out, xnor_8_out, xnor_9_out, xnor_10_out);
  or or_3 (or_3_out, and_3_out, and_5_out);
  or or_4 (useNewPC, branchlogic_1_usenewpc, or_1_out);
  not not_1 (stallWE, or_3_out);
  or or_5 (DXnop, useNewPC, or_3_out);

  // Notes on the sheet:
  //   Branch Logic
  //   LSB to MSB:
  //   SB, LB, BGEU, BLTU, BGE,
  //   BLT, BNE, BEQ, JALR, JAL
  //   SW, LW
  //   Stall Logic
  //   x0 detection
  //   x0 detection
  //   if JAL or JALR
  //   if LB or LW
  //   need new PC if branch or jump
  //   also is a nop control for FD
  //   zap DX or inject bubble if stalling
  //   stall control; 1 if no stall and F/D, PC reg should write
endmodule

module BranchLogic (
  input  [31:0] A,
  input  [31:0] B,
  input  [11:0] tableB,
  output useNewPC
);

  wire and_1_out, and_2_out, and_3_out, and_4_out, and_5_out, and_6_out, and_7_out, and_8_out,
       comparator_1_eq, comparator_1_gt, comparator_1_lt, comparator_2_eq, comparator_2_gt, comparator_2_lt,
       or_1_out, or_2_out;

  Comparator #(.width(32)) comparator_1 (
    .a(A), .b(B), .gt(comparator_1_gt), .eq(comparator_1_eq), .lt(comparator_1_lt));
  Comparator #(.width(32), .mode("unsigned")) comparator_2 (
    .a(A), .b(B), .gt(comparator_2_gt), .eq(comparator_2_eq), .lt(comparator_2_lt));
  and and_1 (and_1_out, comparator_1_gt, tableB[6]);
  and and_2 (and_2_out, comparator_1_gt, tableB[4]);
  and and_3 (and_3_out, comparator_1_eq, tableB[7]);
  and and_4 (and_4_out, comparator_1_eq, tableB[5]);
  and and_5 (and_5_out, comparator_1_lt, tableB[5]);
  and and_6 (and_6_out, comparator_2_gt, tableB[2]);
  and and_7 (and_7_out, comparator_2_eq, tableB[2]);
  and and_8 (and_8_out, tableB[3], comparator_2_lt);
  or or_1 (or_1_out, and_1_out, and_2_out);
  or or_2 (or_2_out, and_3_out, and_4_out);
  or or_3 (useNewPC, or_1_out, or_2_out, and_5_out, and_6_out, and_7_out, and_8_out);

  // Notes on the sheet:
  //   signed
  //   unsigned
  //   A > B
  //   A == B
  //   A < B
  //   A > B
  //   A == B
  //   A < B
endmodule

module Decrement_PC (
  input  [31:0] PC,
  output [31:0] PCout
);


  // Notes on the sheet:
  //   decrement by four bytes
endmodule

module MemFlags (
  input  [11:0] TableB,
  output ld,
  output str
);

  or or_1 (str, TableB[0], TableB[10]);
  or or_2 (ld, TableB[1], TableB[11]);
endmodule

module Compare (
  input  [31:0] A,
  input  [31:0] B,
  input  [31:0] imm,
  input  useImm,
  input  SetSign,
  output [31:0] result
);

  wire comparator_black_box_1_p4;
  wire [31:0] comparator_black_box_1_p2;

  // Comparator_Black_Box comparator_black_box_1: pin names not known; wires that end beside it: A, comparator_black_box_1_p2, SetSign, comparator_black_box_1_p4, result
  Multiplexer #(.width(32), .enable("false")) multiplexer_1 (
    .in0(B), .in1(imm), .out(comparator_black_box_1_p2), .sel(useImm));
  assign result = {{31{1'b0}}, comparator_black_box_1_p4};  // Bit_Extender bit_extender_1
endmodule

module FD (
  input  [31:0] inst,
  input  [31:0] PC,
  input  nop,
  input  stallWE,
  input  clk,
  output [31:0] instOut,
  output [31:0] PCout
);

  wire [2:0] bit_extender_2_out, or_1_out;
  wire [31:0] and_1_out, bit_extender_1_out;

  assign bit_extender_1_out = {{31{nop}}, nop};  // Bit_Extender bit_extender_1
  assign and_1_out = inst & ~bit_extender_1_out;  // AND_Gate and_1, 32 bits wide
  assign or_1_out = {and_1_out[4], and_1_out[1:0]} | bit_extender_2_out;  // OR_Gate or_1, 3 bits wide
  assign bit_extender_2_out = {{2{nop}}, nop};  // Bit_Extender bit_extender_2
  Register #(.width(32)) IF_DE_instr (
    .D({and_1_out[31:5], or_1_out[2], and_1_out[3:2], or_1_out[1:0]}), .en(stallWE), .clk(clk), .Q(instOut));  // open: clr
  Register #(.width(32)) IF_DE_PC (.D(PC), .en(stallWE), .clk(clk), .Q(PCout));  // open: clr

  // Notes on the sheet:
  //   step 1: clear inst on nop
  //   step 2: on nop add bits
  //   defining ADDI x0, x0, 0
endmodule

module DX (
  input  [31:0] A,
  input  [31:0] B,
  input  [4:0] rs1,
  input  [4:0] rs1_2,
  input  [4:0] rd,
  input  [31:0] imm,
  input  useImm,
  input  [3:0] ALUop,
  input  regWE,
  input  set,
  input  shiftRegVal,
  input  setSign,
  input  AUIPC,
  input  [11:0] tableB,
  input  ZeroOutA,
  input  [3:0] selectBytes,
  input  [31:0] PC,
  input  [31:0] nextPC,
  input  nop,
  input  clk,
  output [31:0] Aout,
  output [31:0] Bout,
  output [4:0] rs1out,
  output [4:0] rs1out_2,
  output [4:0] rdOut,
  output [31:0] immOut,
  output useImmOut,
  output [3:0] ALUopOut,
  output regWEout,
  output setOut,
  output shiftRegValOut,
  output setSignOut,
  output AUIPCout,
  output [11:0] tableBout,
  output ZeroOutAout,
  output [3:0] selectBytesOut,
  output [31:0] PCout,
  output [31:0] nextPCout
);

  wire and_1_out;
  wire [3:0] and_3_out, bit_extender_2_out;
  wire [11:0] and_2_out, bit_extender_1_out;

  assign bit_extender_1_out = {{11{nop}}, nop};  // Bit_Extender bit_extender_1
  assign bit_extender_2_out = {{3{nop}}, nop};  // Bit_Extender bit_extender_2
  Register #(.width(32)) register_1 (.D(A), .clk(clk), .Q(Aout));  // open: en, clr
  Register #(.width(32)) register_2 (.D(B), .clk(clk), .Q(Bout));  // open: en, clr
  Register #(.width(5)) register_3 (.D(rs1), .clk(clk), .Q(rs1out));  // open: en, clr
  Register #(.width(5)) register_4 (.D(rs1_2), .clk(clk), .Q(rs1out_2));  // open: en, clr
  Register #(.width(5)) register_5 (.D(rd), .clk(clk), .Q(rdOut));  // open: en, clr
  Register #(.width(32)) register_6 (.D(imm), .clk(clk), .Q(immOut));  // open: en, clr
  Register #(.width(1)) register_7 (.D(useImm), .clk(clk), .Q(useImmOut));  // open: en, clr
  Register #(.width(4)) register_8 (.D(ALUop), .clk(clk), .Q(ALUopOut));  // open: en, clr
  Register #(.width(1)) register_9 (.D(and_1_out), .clk(clk), .Q(regWEout));  // open: en, clr
  and and_1 (and_1_out, regWE, ~nop);  // AND_Gate
  Register #(.width(1)) register_10 (.D(set), .clk(clk), .Q(setOut));  // open: en, clr
  Register #(.width(1)) register_11 (.D(shiftRegVal), .clk(clk), .Q(shiftRegValOut));  // open: en, clr
  Register #(.width(1)) register_12 (.D(setSign), .clk(clk), .Q(setSignOut));  // open: en, clr
  Register #(.width(1)) register_13 (.D(AUIPC), .clk(clk), .Q(AUIPCout));  // open: en, clr
  Register #(.width(12)) register_14 (.D(and_2_out), .clk(clk), .Q(tableBout));  // open: en, clr
  assign and_2_out = tableB & ~bit_extender_1_out;  // AND_Gate and_2, 12 bits wide
  Register #(.width(1)) register_15 (.D(ZeroOutA), .clk(clk), .Q(ZeroOutAout));  // open: en, clr
  Register #(.width(4)) register_16 (.D(and_3_out), .clk(clk), .Q(selectBytesOut));  // open: en, clr
  assign and_3_out = selectBytes & ~bit_extender_2_out;  // AND_Gate and_3, 4 bits wide
  Register #(.width(32)) register_17 (.D(PC), .clk(clk), .Q(PCout));  // open: en, clr
  Register #(.width(32)) register_18 (.D(nextPC), .clk(clk), .Q(nextPCout));  // open: en, clr

  // Notes on the sheet:
  //   nop generator part 1: disable all memory access
  //   nop generator part 2: prevent branches from being taken
  //   nop generator part 3: disable all memory access
  //   nop control; 1 = nop i.e. no mem or reg file access
endmodule

module XM (
  input  [31:0] result,
  input  [4:0] rd,
  input  regWE,
  input  [3:0] selectBytes,
  input  ldFlag,
  input  strFlag,
  input  [31:0] data,
  input  clk,
  output [31:0] resultOut,
  output [4:0] rdOut,
  output regWEout,
  output [3:0] selectBytesOut,
  output ldFlagOut,
  output strFlagout,
  output [31:0] dataOut
);

  Register #(.width(32)) EX_M_Result (.D(result), .clk(clk), .Q(resultOut));  // open: en, clr
  Register #(.width(5)) EX_M_rd (.D(rd), .clk(clk), .Q(rdOut));  // open: en, clr
  Register #(.width(1)) EX_M_regWE (.D(regWE), .clk(clk), .Q(regWEout));  // open: en, clr
  Register #(.width(4)) EX_M_SelectBytes (.D(selectBytes), .clk(clk), .Q(selectBytesOut));  // open: en, clr
  Register #(.width(1)) EX_M_ld (.D(ldFlag), .clk(clk), .Q(ldFlagOut));  // open: en, clr
  Register #(.width(1)) EX_M_str (.D(strFlag), .clk(clk), .Q(strFlagout));  // open: en, clr
  Register #(.width(32)) EX_M_Data (.D(data), .clk(clk), .Q(dataOut));  // open: en, clr
endmodule

module MW (
  input  [31:0] result,
  input  [31:0] data,
  input  regWE,
  input  [4:0] rd,
  input  ldFlag,
  input  clk,
  output [31:0] resultOut,
  output [31:0] dataOut,
  output regWEout,
  output [4:0] rdOut,
  output dataCtrl
);

  Register #(.width(32)) M_W_Result (.D(result), .clk(clk), .Q(resultOut));  // open: en, clr
  Register #(.width(32)) M_W_Data (.D(data), .clk(clk), .Q(dataOut));  // open: en, clr
  Register #(.width(1)) M_W_regWE (.D(regWE), .clk(clk), .Q(regWEout));  // open: en, clr
  Register #(.width(5)) M_W_rd (.D(rd), .clk(clk), .Q(rdOut));  // open: en, clr
  Register #(.width(1)) M_W_ldFlag (.D(ldFlag), .clk(clk), .Q(dataCtrl));  // open: en, clr
endmodule

module computeAddress (
  input  [3:0] selectBytes,
  input  [31:0] resultOut,
  output [3:0] selectBytesOut,
  output [19:0] address
);

  wire or_1_out;
  wire [3:0] bit_extender_1_out;

  or or_1 (or_1_out, resultOut[20], resultOut[21], resultOut[22], resultOut[23], resultOut[24], resultOut[25], resultOut[26], resultOut[27], resultOut[28], resultOut[29], resultOut[30], resultOut[31]);
  assign bit_extender_1_out = {{3{or_1_out}}, or_1_out};  // Bit_Extender bit_extender_1
  assign selectBytesOut = selectBytes & ~bit_extender_1_out;  // AND_Gate and_1, 4 bits wide

  assign address = resultOut[19:0];

  // Notes on the sheet:
  //   1 if selectBits should be 0 (no write or read)
  //   set selectBytes to all 0 if invalid memory address
endmodule

module test (
  input  [31:0] in_1,
  input  [11:0] in_2,
  output [11:0] out_3
);

  wire or_1_out;

  or or_1 (or_1_out, in_2[0], in_2[10]);
  Multiplexer #(.width(5), .enable("false")) multiplexer_1 (
    .in0(in_1[24:20]), .in1(in_1[11:7]), .out(out_3[4:0]), .sel(or_1_out));

  assign out_3[11:5] = in_1[31:25];

  // Notes on the sheet:
  //   LSB to MSB:
  //   SB, LB, BGEU, BLTU, BGE,
  //   BLT, BNE, BEQ, JALR, JAL
  //   SW, LW
  //   if load
  //   if store
  //   if store
endmodule

module loadAndSaveImm (
  input  [31:0] instBits,
  input  [11:0] tableB,
  output [11:0] imm
);

  wire or_1_out;

  or or_1 (or_1_out, tableB[0], tableB[10]);
  Multiplexer #(.width(5), .enable("false")) multiplexer_1 (
    .in0(instBits[24:20]), .in1(instBits[11:7]), .out(imm[4:0]), .sel(or_1_out));

  assign imm[11:5] = instBits[31:25];

  // Notes on the sheet:
  //   LSB to MSB:
  //   SB, LB, BGEU, BLTU, BGE,
  //   BLT, BNE, BEQ, JALR, JAL
  //   SW, LW
  //   if load
  //   if store
  //   fill in 11 to 5 with same 31 to 25
  //   if store
endmodule

module getRegWE (
  input  tableAregWE,
  input  [11:0] tableB,
  output regWE
);

  wire or_1_out, or_2_out;

  or or_1 (or_1_out, tableB[11], tableB[8], tableB[9], tableB[1]);
  Multiplexer #(.enable("false")) multiplexer_1 (.in0(tableAregWE), .in1(or_1_out), .out(regWE), .sel(or_2_out));
  or or_2 (or_2_out, tableB[0], tableB[1], tableB[2], tableB[3], tableB[4], tableB[5], tableB[6], tableB[7], tableB[8], tableB[9], tableB[10], tableB[11]);

  // Notes on the sheet:
  //   LSB to MSB:
  //   SB, LB, BGEU, BLTU, BGE,
  //   BLT, BNE, BEQ, JALR, JAL
  //   SW, LW
  //   if any valid table B instruction is present
  //   The only table B instructions with reg file access are jumps and loads
endmodule

module jumpHandler (
  input  [31:0] result,
  input  [11:0] tableBOneHot,
  input  [31:0] nextPC,
  output [31:0] branchTarget,
  output [31:0] resultOut
);

  wire or_1_out;

  and and_1 (branchTarget[0], result[0], ~tableBOneHot[8]);  // AND_Gate
  or or_1 (or_1_out, tableBOneHot[8], tableBOneHot[9]);
  Multiplexer #(.width(32), .enable("false")) multiplexer_1 (
    .in0({result[31:1], branchTarget[0]}), .in1(nextPC), .out(resultOut), .sel(or_1_out));

  assign branchTarget[31:1] = result[31:1];

  // Notes on the sheet:
  //   PC of this inst + 4
  //   from ALU
  //   JALR = 8
  //   JAL = 9
  //   Set LSB of JALR imm + rs1 result to 0
  //   if any jump
  //   if jump, send PC+4 to register
endmodule

module SignExtendLB (
  input  [31:0] Data,
  input  ld,
  input  [3:0] selectBytes,
  output [31:0] dataOut
);

  wire and_1_out, and_2_out;
  wire [31:0] bit_extender_1_out;

  and and_1 (and_1_out, ld, and_2_out);
  and and_2 (and_2_out, selectBytes[0], ~selectBytes[1], ~selectBytes[2], ~selectBytes[3]);  // AND_Gate
  assign bit_extender_1_out = {{24{Data[7]}}, Data[7:0]};  // Bit_Extender bit_extender_1
  Multiplexer #(.width(32), .enable("false")) multiplexer_1 (
    .in0(Data), .in1(bit_extender_1_out), .out(dataOut), .sel(and_1_out));

  // Notes on the sheet:
  //   if loading
  //   if LB
endmodule
